# Fritzing sketch Full Design (saved by Fritzing 0.9.3b)

parts:
  KY-2 = Keyes Relay [package=THT]
  Part1 = Arduino Uno (Rev3)
  PS1 = prefix0000 [part_number=S-350-60]
  M1 = DC Motor
  T1 = LM35 Temperature Sensor [package="TO92 [THT]"]
  U1 = ESP8266 WiFi Module [part_number=ESP8266]
  JACK1 = 2.1mm Barrel Jack with Terminal Block  # not connected

nets:
  N1: KY-2.signal, PS1.connector0
  N2: KY-2.power, PS1.connector3
  N3: KY-2.ground, Part1.D13/SCK
  N4: KY-2.NO, M1.pin_2
  N5: Part1.A0, T1.Vout
  N6: Part1.D2, U1.TXD
  N7: Part1.D3_PWM, U1.RXD
  N8: Part1.3V3, U1.CH_PD
  N9: Part1.5V, T1.+Vs

notes:
  Motor Pompa AC
  Hubungan ke PLN
  Urutan koneksi
  VCC - GND - IN
  Beberapa PSU kadang urutannya berbeda.
  Jadi perhatikan Simbol pada power supply

custom parts:
  Keyes Relay: The Keyes 5V relay module is suitable for SCM development, home appliance control. It uses a 5V~12V TIL control signal which can control DC / AC signal.
  ESP8266 WiFi Module: Generic WiFi Module based on the ESP8266 with onboard PCB antenna and UART communications
